# Fritzing sketch MiHomeNode (saved by Fritzing 0.9.3b)
breadboards: 1

parts:
  Node = Arduino Nano (Rev3.0)
  SHT31 = Adafruit SHT31-D Sensirion Temperature/Humidity Sensor [part_number="Adafruit #2857"]
  TSL = Adafruit TSL2561 [part_number="Adafruit #439"]
  UV = SI1145 Digital UV Index + IR + Visible Light Sensor [part_number=1777]
  SDA = Resistor [tolerance=±5% resistance=4.7k package=THT]
  SCL = Resistor [tolerance=±5% resistance=4.7k package=THT]
  Radio = Adafruit RFM69HCW Transceiver Radio [part_number="Adafruit #3070 and #3071"]
  ANT = Antenna
  CCS811 = Adafruit CCS811

nets:
  GND: Node.GND, Radio.GND
  N1: Node.D2, Radio.RST
  N2: Node.D3, Radio.DIO0
  N3: Node.D4, Radio.CS
  N4: Node.D11/MOSI, Radio.MOSI
  N5: Node.D12/MISO, Radio.MISO
  N6: Node.A5, SCL.Pin_0
  N7: Node.A4, SDA.Pin_0
  3V3: Node.3V3, UV.+3V3, Radio.VIN
  N8: Node.D13/SCK, Radio.SCK
  VIN: SHT31.VIN, TSL.3.3V, CCS811.VIN
  GND_2: SHT31.GND, TSL.GND, UV.GND, CCS811.GND
  N9: SHT31.SCL, TSL.SCL, UV.SCL, SCL.Pin_1, CCS811.SCL
  N10: SHT31.SDA, TSL.SDA, UV.SDA, SDA.Pin_1, CCS811.SDA
  N11: Radio.ANTENNA, ANT.antenna_lead

custom parts:
  Adafruit SHT31-D Sensirion Temperature/Humidity Sensor: Sensirion Temperature/Humidity sensors are some of the finest & highest-accuracy devices you can get. And, finally we have some that have a true I2C interface for easy reading. The SHT31-D sensor has an excellent ±2% relative humidity and ±0.3°C accuracy for most uses. Unlike earlier SHT sensors, this sensor has a true I2C interface, and (bonus!) even with two address options. It also is 3V or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
  Adafruit TSL2561: The TSL2561 luminosity sensor is an advanced digital light sensor, ideal for use in a wide range of light situations. Compared to low cost CdS cells, this sensor is more precise, allowing for exact lux calculations and can be configured for different gain/timing ranges to detect light ranges from up to 0.1 - 40,000+ Lux on the fly. The best part of this sensor is that it contains both infrared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
  SI1145 Digital UV Index + IR + Visible Light Sensor: The SI1145 is a new sensor from SiLabs with a calibrated light sensing algorithm that can calculate UV Index. It doesn't contain an actual UV sensing element, instead it approximates it based on visible & IR light from the sun. We took this outside a couple days and compared the calculated UV index with the news-reported index and found it was very accurate! It's a digital sensor that works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
  Adafruit RFM69HCW Transceiver Radio: Sending data over long distances is like magic, and now you can be a magician with this range of powerful and easy-to-use radio modules. Sure, sometimes you want to talk to a computer (a good time to use WiFi) or perhaps communicate with a Phone (choose Bluetooth Low Energy!) but what if you want to send data very far? Most WiFi, Bluetooth, Zigbee and other wireless chipsets use 2.4GHz, which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
